# Fritzing sketch hardware (saved by Fritzing 0.8.7b)
breadboards: 1

parts:
  For_WTS_sample_client = Arduino Uno (Rev3)
  LED1 = LED - 5mm [color="Red (633nm)" package="5 mm [THT]"]
  R1 = Resistor [tolerance=±5% resistance=330 package=THT]
  S1 = Pushbutton [package=THT]
  R2 = Resistor [tolerance=±5% resistance=10k package=THT]
  photo-resistor = Photocell (LDR) [package=THT]

nets:
  N1: For_WTS_sample_client.A0, R2.Pin_1, photo-resistor.pin_0
  N2: For_WTS_sample_client.D8, R1.Pin_0
  N3: For_WTS_sample_client.D9_PWM, S1.leg1
  GND: For_WTS_sample_client.GND, LED1.cathode, S1.leg0, R2.Pin_0
  N4: For_WTS_sample_client.5V, photo-resistor.pin_1
  N5: LED1.anode, R1.Pin_1
